# Fritzing sketch peppersorter (saved by Fritzing 0.9.2b)
breadboards: 1

parts:
  Raspberry_Pi1 = Raspberry Pi 2
  J1 = Basic Servo
  S1 = Momentary Switch [package=ksa_sealed_tac_switch]
  S2 = Momentary Switch [package=ksa_sealed_tac_switch]
  S3 = Round Pushbutton
  LED2 = LEDs [package=led10mm]
  LED3 = LEDs [package=led10mm]
  LED4 = LEDs [package=led10mm]
  R1 = Resistor [tolerance=±5% resistance=220 package="0603 [SMD]"]
  R2 = Resistor [tolerance=±5% resistance=220 package="0603 [SMD]"]
  R3 = Resistor [tolerance=±5% resistance=220 package="0603 [SMD]"]
  R4 = Resistor [tolerance=±5% resistance=220 package="0603 [SMD]"]
  Q1 = npn-Powertransistor [package="TO220 [THT]"]
  J2 = Basic Servo
  VCC1 = 4 x AAA Battery Mount
  U1 = TRANSCHIPTC5747 [package=camera_sfv24r-2st_2]  # not connected
  LED5 = LEDs [package=led10mm]
  R5 = Resistor [tolerance=±5% resistance=2.2k package="0603 [SMD]"]

nets (from the schematic view):
  3V3: Raspberry_Pi1.3v3, Raspberry_Pi1.3V3, S1.1, S1.2, S2.1, S2.2, S3.leg0
  N1: Raspberry_Pi1.GPIO4, S3.leg1
  N2: Raspberry_Pi1.GPIO17, S1.3, S1.4
  N3: Raspberry_Pi1.GPIO27, S2.3, S2.4
  GND: Raspberry_Pi1.GND, J1.gnd, R1.Pin_1, R2.Pin_0, R3.Pin_0, R4.Pin_0, Q1.emitter, VCC1.-
  N4: Raspberry_Pi1.GPIO25, J1.pulse
  N5: Raspberry_Pi1.GPIO24, J2.pulse
  N6: Raspberry_Pi1.GPIO23, R5.Pin_0
  VCC: J1.vcc, J2.vcc
  N7: LED2.A, LED3.A, LED4.A, VCC1.+, LED5.A
  N8: LED2.C, R2.Pin_1
  N9: LED3.C, R1.Pin_0
  N10: LED4.C, R4.Pin_1
  N11: R3.Pin_1, LED5.C
  N12: Q1.base, R5.Pin_1
  N13: Q1.collector, J2.gnd
